# Fritzing sketch projektSchemaFritz (saved by Fritzing 0.9.3b)
circuit board: 8.46667cm x 5.64444cm
breadboards: 1

parts:
  Arduino_Nano = Arduino Nano (Rev3.0)
  LED1 = LED - 5mm [color="Green (555nm)" package="5 mm [THT]"]
  LED2 = LED - 5mm [color="Yellow (585nm)" package="5 mm [THT]"]
  LED3 = LED - 5mm [color="Red (633nm)" package="5 mm [THT]"]
  Grove1 = Grove 4 Digit Display
  S1 = Pushbutton [package="[SMD]"]
  LED4 = LED - 5mm [color="Red (633nm)" package="5 mm [THT]"]
  LED5 = LED - 5mm [color="Green (555nm)" package="5 mm [THT]"]
  R1 = Resistor [tolerance=±5% resistance=300 package=THT]
  HC-SR04_Sensor_1 = HC-SR04 Ultrasonic Distance Sensor
  J1 = Piezo Speaker

nets (from the breadboard view):
  GND: Arduino_Nano.GND, LED1.cathode, LED2.cathode, LED3.cathode, Grove1.GND, S1.Pin_3, S1.Pin_4, R1.Pin_0, HC-SR04_Sensor_1.GND
  N1: Arduino_Nano.D2, J1.pin2
  N2: Arduino_Nano.D3, Grove1.DIO
  N3: Arduino_Nano.D4, Grove1.CLK
  N4: Arduino_Nano.D5, LED3.anode
  N5: Arduino_Nano.D6, LED2.anode
  N6: Arduino_Nano.D7, LED1.anode
  N7: Arduino_Nano.D8, S1.Pin_1, S1.Pin_2
  N8: Arduino_Nano.D9, HC-SR04_Sensor_1.ECHO
  N9: Arduino_Nano.D10, HC-SR04_Sensor_1.TRIG
  N10: Arduino_Nano.D11/MOSI, LED5.anode
  N11: Arduino_Nano.D12/MISO, LED4.anode
  VCC: Arduino_Nano.5V, Grove1.VCC, LED4.cathode, LED5.cathode, HC-SR04_Sensor_1.VCC
  N12: R1.Pin_1, J1.pin1
